// Logisim project TheLife.circ as structural Verilog: 7 circuits, main circuit Cell
module main (
  input  [14:0] Pressed_1,
  input  [14:0] Pressed_1_2,
  input  [14:0] Pressed_1_3,
  input  [14:0] Pressed_1_4,
  input  [14:0] Pressed_1_5,
  input  [14:0] Pressed_1_6,
  input  [14:0] Pressed_1_7,
  input  [14:0] Pressed_1_8,
  input  [14:0] Pressed_1_9,
  input  [14:0] Pressed_1_10,
  input  [14:0] Pressed_1_11,
  input  [14:0] Pressed_1_12,
  input  [14:0] Pressed_1_13,
  input  [14:0] Pressed_1_14,
  input  [14:0] Pressed_1_15
);

  wire clock_1_out;
  wire [14:0] rowsplate_1_out_1, rowsplate_1_out_2, rowsplate_1_out_3, rowsplate_1_out_4, rowsplate_1_out_5,
       rowsplate_1_out_6, rowsplate_1_out_7, rowsplate_1_out_8, rowsplate_1_out_9, rowsplate_1_out_10,
       rowsplate_1_out_11, rowsplate_1_out_12, rowsplate_1_out_13, rowsplate_1_out_14, rowsplate_1_out_15;

  Clock clock_1 (.out(clock_1_out));
  DotMatrix #(.matrixcols(15), .matrixrows(15)) dotmatrix_1 (
    .col0(rowsplate_1_out_1), .col1(rowsplate_1_out_2), .col2(rowsplate_1_out_3), .col3(rowsplate_1_out_4),
    .col4(rowsplate_1_out_5), .col5(rowsplate_1_out_6), .col6(rowsplate_1_out_7), .col7(rowsplate_1_out_8),
    .col8(rowsplate_1_out_9), .col9(rowsplate_1_out_10), .col10(rowsplate_1_out_11),
    .col11(rowsplate_1_out_12), .col12(rowsplate_1_out_13), .col13(rowsplate_1_out_14),
    .col14(rowsplate_1_out_15));
  RowsPlate rowsplate_1 (
    .tick(clock_1_out), .Pressed_1(Pressed_1), .Pressed_2(Pressed_1_2), .Pressed_3(Pressed_1_3),
    .Pressed_4(Pressed_1_4), .Pressed_5(Pressed_1_5), .Pressed_6(Pressed_1_6), .Pressed_7(Pressed_1_7),
    .Pressed_8(Pressed_1_8), .Pressed_9(Pressed_1_9), .Pressed_10(Pressed_1_10), .Pressed_11(Pressed_1_11),
    .Pressed_12(Pressed_1_12), .Pressed_13(Pressed_1_13), .Pressed_14(Pressed_1_14),
    .Pressed_15(Pressed_1_15), .out_1(rowsplate_1_out_1), .out_2(rowsplate_1_out_2),
    .out_3(rowsplate_1_out_3), .out_4(rowsplate_1_out_4), .out_5(rowsplate_1_out_5),
    .out_6(rowsplate_1_out_6), .out_7(rowsplate_1_out_7), .out_8(rowsplate_1_out_8),
    .out_9(rowsplate_1_out_9), .out_10(rowsplate_1_out_10), .out_11(rowsplate_1_out_11),
    .out_12(rowsplate_1_out_12), .out_13(rowsplate_1_out_13), .out_14(rowsplate_1_out_14),
    .out_15(rowsplate_1_out_15));
endmodule

module Cell (
  input  upper_center,
  input  upper_left,
  input  upper_right,
  input  left,
  input  right,
  input  bottom_left,
  input  bottom_right,
  input  bottom_center,
  input  tick,
  input  waspressed,
  output State
);

  State_manager state_manager_1 (
    .nb1(upper_center), .nb2(upper_left), .nb3(upper_right), .nb4(left), .nb5(right), .nb6(bottom_left),
    .nb7(bottom_right), .nb8(bottom_center), .user_s_hand(tick), .tick(waspressed), .State(State));
endmodule

module State_manager (
  input  nb1,
  input  nb2,
  input  nb3,
  input  nb4,
  input  nb5,
  input  nb6,
  input  nb7,
  input  nb8,
  input  user_s_hand,
  input  tick,
  output State
);

  wire and_1_out, and_2_out, and_3_out, and_4_out, and_5_out, not_1_out, not_2_out, not_3_out, not_4_out,
       or_1_out, or_2_out, or_3_out;
  wire [1:0] adder_1_out, adder_2_out, adder_3_out, adder_4_out, adder_5_out, adder_6_out;
  wire [2:0] adder_7_out;
  wire [2:2] adder_5_cout, adder_6_cout;

  Adder #(.width(1)) adder_1 (.a(nb1), .b(nb2), .out(adder_1_out[0]), .cout(adder_1_out[1]));  // open: cin
  Adder #(.width(1)) adder_2 (.a(nb3), .b(nb4), .out(adder_2_out[0]), .cout(adder_2_out[1]));  // open: cin
  Adder #(.width(1)) adder_3 (.a(nb5), .b(nb6), .out(adder_3_out[0]), .cout(adder_3_out[1]));  // open: cin
  Adder #(.width(1)) adder_4 (.a(nb7), .b(nb8), .out(adder_4_out[0]), .cout(adder_4_out[1]));  // open: cin
  Adder #(.width(2)) adder_5 (
    .a(adder_1_out), .b(adder_2_out), .out(adder_5_out), .cout(adder_5_cout[2]));  // open: cin
  Adder #(.width(2)) adder_6 (
    .a(adder_3_out), .b(adder_4_out), .out(adder_6_out), .cout(adder_6_cout[2]));  // open: cin
  Adder #(.width(3)) adder_7 (
    .a({adder_5_cout[2], adder_5_out}), .b({adder_6_cout[2], adder_6_out}), .out(adder_7_out));  // open: cin, cout
  not not_1 (not_1_out, adder_7_out[2]);
  not not_2 (not_2_out, adder_7_out[0]);
  and and_1 (and_1_out, adder_7_out[0], adder_7_out[1], not_1_out);
  and and_2 (and_2_out, not_1_out, adder_7_out[1], not_2_out);
  or or_1 (or_1_out, user_s_hand, tick);
  not not_3 (not_3_out, user_s_hand);
  or or_2 (or_2_out, and_1_out, and_2_out);
  not not_4 (not_4_out, State);
  and and_3 (and_3_out, and_1_out, not_4_out, not_3_out);
  and and_4 (and_4_out, not_3_out, State, or_2_out);
  and and_5 (and_5_out, user_s_hand, not_4_out);
  or or_3 (or_3_out, and_3_out, and_4_out, and_5_out);
  Register #(.width(1), .trigger("falling")) register_1 (.D(or_3_out), .Q(State), .clk(or_1_out));  // open: en, clr

  // Notes on the sheet:
  //   3 живые
  //   2 живые
  //   Команда на смену состояния
  //   Оживание по правилам + нет команд от юзера
  //   Отрицание для смены состояния
  //   Продолжение существования
endmodule

module Displaying_cells (
);

  Cell cell_1 ();  // open: upper_center, upper_left, upper_right, left, right, bottom_left, bottom_right, bottom_center, tick, waspressed, State
endmodule

module Row_of_cells (
  input  [14:0] Up,
  input  tick,
  input  [14:0] Down,
  input  [14:0] Pressed,
  output [14:0] Display
);

  Cell cell_1 (
    .upper_center(Up[0]), .upper_left(Up[14]), .upper_right(Up[1]), .left(Display[14]), .right(Display[1]),
    .bottom_left(Down[14]), .bottom_right(Down[1]), .bottom_center(Down[0]), .tick(Pressed[0]),
    .waspressed(tick), .State(Display[0]));
  Cell cell_2 (
    .upper_center(Up[1]), .upper_left(Up[0]), .upper_right(Up[2]), .left(Display[0]), .right(Display[2]),
    .bottom_left(Down[0]), .bottom_right(Down[2]), .bottom_center(Down[1]), .tick(Pressed[1]),
    .waspressed(tick), .State(Display[1]));
  Cell cell_3 (
    .upper_center(Up[2]), .upper_left(Up[1]), .upper_right(Up[3]), .left(Display[1]), .right(Display[3]),
    .bottom_left(Down[1]), .bottom_right(Down[3]), .bottom_center(Down[2]), .tick(Pressed[2]),
    .waspressed(tick), .State(Display[2]));
  Cell cell_4 (
    .upper_center(Up[3]), .upper_left(Up[2]), .upper_right(Up[4]), .left(Display[2]), .right(Display[4]),
    .bottom_left(Down[2]), .bottom_right(Down[4]), .bottom_center(Down[3]), .tick(Pressed[3]),
    .waspressed(tick), .State(Display[3]));
  Cell cell_5 (
    .upper_center(Up[4]), .upper_left(Up[3]), .upper_right(Up[5]), .left(Display[3]), .right(Display[5]),
    .bottom_left(Down[3]), .bottom_right(Down[5]), .bottom_center(Down[4]), .tick(Pressed[4]),
    .waspressed(tick), .State(Display[4]));
  Cell cell_6 (
    .upper_center(Up[5]), .upper_left(Up[4]), .upper_right(Up[6]), .left(Display[4]), .right(Display[6]),
    .bottom_left(Down[4]), .bottom_right(Down[6]), .bottom_center(Down[5]), .tick(Pressed[5]),
    .waspressed(tick), .State(Display[5]));
  Cell cell_7 (
    .upper_center(Up[6]), .upper_left(Up[5]), .upper_right(Up[7]), .left(Display[5]), .right(Display[7]),
    .bottom_left(Down[5]), .bottom_right(Down[7]), .bottom_center(Down[6]), .tick(Pressed[6]),
    .waspressed(tick), .State(Display[6]));
  Cell cell_8 (
    .upper_center(Up[7]), .upper_left(Up[6]), .upper_right(Up[8]), .left(Display[6]), .right(Display[8]),
    .bottom_left(Down[6]), .bottom_right(Down[8]), .bottom_center(Down[7]), .tick(Pressed[7]),
    .waspressed(tick), .State(Display[7]));
  Cell cell_9 (
    .upper_center(Up[8]), .upper_left(Up[7]), .upper_right(Up[9]), .left(Display[7]), .right(Display[9]),
    .bottom_left(Down[7]), .bottom_right(Down[9]), .bottom_center(Down[8]), .tick(Pressed[8]),
    .waspressed(tick), .State(Display[8]));
  Cell cell_10 (
    .upper_center(Up[9]), .upper_left(Up[8]), .upper_right(Up[10]), .left(Display[8]), .right(Display[10]),
    .bottom_left(Down[8]), .bottom_right(Down[10]), .bottom_center(Down[9]), .tick(Pressed[9]),
    .waspressed(tick), .State(Display[9]));
  Cell cell_11 (
    .upper_center(Up[10]), .upper_left(Up[9]), .upper_right(Up[11]), .left(Display[9]), .right(Display[11]),
    .bottom_left(Down[9]), .bottom_right(Down[11]), .bottom_center(Down[10]), .tick(Pressed[10]),
    .waspressed(tick), .State(Display[10]));
  Cell cell_12 (
    .upper_center(Up[11]), .upper_left(Up[10]), .upper_right(Up[12]), .left(Display[10]),
    .right(Display[12]), .bottom_left(Down[10]), .bottom_right(Down[12]), .bottom_center(Down[11]),
    .tick(Pressed[11]), .waspressed(tick), .State(Display[11]));
  Cell cell_13 (
    .upper_center(Up[12]), .upper_left(Up[11]), .upper_right(Up[13]), .left(Display[11]),
    .right(Display[13]), .bottom_left(Down[11]), .bottom_right(Down[13]), .bottom_center(Down[12]),
    .tick(Pressed[12]), .waspressed(tick), .State(Display[12]));
  Cell cell_14 (
    .upper_center(Up[13]), .upper_left(Up[12]), .upper_right(Up[14]), .left(Display[12]),
    .right(Display[14]), .bottom_left(Down[12]), .bottom_right(Down[14]), .bottom_center(Down[13]),
    .tick(Pressed[13]), .waspressed(tick), .State(Display[13]));
  Cell cell_15 (
    .upper_center(Up[14]), .upper_left(Up[13]), .upper_right(Up[0]), .left(Display[13]), .right(Display[0]),
    .bottom_left(Down[13]), .bottom_right(Down[0]), .bottom_center(Down[14]), .tick(Pressed[14]),
    .waspressed(tick), .State(Display[14]));
endmodule

module RowsPlate (
  input  tick,
  input  [14:0] Pressed_1,
  input  [14:0] Pressed_2,
  input  [14:0] Pressed_3,
  input  [14:0] Pressed_4,
  input  [14:0] Pressed_5,
  input  [14:0] Pressed_6,
  input  [14:0] Pressed_7,
  input  [14:0] Pressed_8,
  input  [14:0] Pressed_9,
  input  [14:0] Pressed_10,
  input  [14:0] Pressed_11,
  input  [14:0] Pressed_12,
  input  [14:0] Pressed_13,
  input  [14:0] Pressed_14,
  input  [14:0] Pressed_15,
  output [14:0] out_1,
  output [14:0] out_2,
  output [14:0] out_3,
  output [14:0] out_4,
  output [14:0] out_5,
  output [14:0] out_6,
  output [14:0] out_7,
  output [14:0] out_8,
  output [14:0] out_9,
  output [14:0] out_10,
  output [14:0] out_11,
  output [14:0] out_12,
  output [14:0] out_13,
  output [14:0] out_14,
  output [14:0] out_15
);

  Row_of_cells row_of_cells_1 (.tick(tick), .Pressed(Pressed_1), .Display(out_1), .Up(out_15), .Down(out_2));
  Row_of_cells row_of_cells_2 (.tick(tick), .Pressed(Pressed_2), .Display(out_2), .Up(out_1), .Down(out_3));
  Row_of_cells row_of_cells_3 (.tick(tick), .Pressed(Pressed_3), .Display(out_3), .Up(out_2), .Down(out_4));
  Row_of_cells row_of_cells_4 (.tick(tick), .Pressed(Pressed_4), .Display(out_4), .Up(out_3), .Down(out_5));
  Row_of_cells row_of_cells_5 (.tick(tick), .Pressed(Pressed_5), .Display(out_5), .Up(out_4), .Down(out_6));
  Row_of_cells row_of_cells_6 (.tick(tick), .Pressed(Pressed_6), .Display(out_6), .Up(out_5), .Down(out_7));
  Row_of_cells row_of_cells_7 (.tick(tick), .Pressed(Pressed_7), .Display(out_7), .Up(out_6), .Down(out_8));
  Row_of_cells row_of_cells_8 (.tick(tick), .Pressed(Pressed_8), .Display(out_8), .Up(out_7), .Down(out_9));
  Row_of_cells row_of_cells_9 (.tick(tick), .Pressed(Pressed_9), .Display(out_9), .Up(out_8), .Down(out_10));
  Row_of_cells row_of_cells_10 (.tick(tick), .Pressed(Pressed_10), .Display(out_10), .Up(out_9), .Down(out_11));
  Row_of_cells row_of_cells_11 (.tick(tick), .Pressed(Pressed_11), .Display(out_11), .Up(out_10), .Down(out_12));
  Row_of_cells row_of_cells_12 (.tick(tick), .Pressed(Pressed_12), .Display(out_12), .Up(out_11), .Down(out_13));
  Row_of_cells row_of_cells_13 (.tick(tick), .Pressed(Pressed_13), .Display(out_13), .Up(out_12), .Down(out_14));
  Row_of_cells row_of_cells_14 (.tick(tick), .Pressed(Pressed_14), .Display(out_14), .Up(out_13), .Down(out_15));
  Row_of_cells row_of_cells_15 (.tick(tick), .Pressed(Pressed_15), .Display(out_15), .Up(out_14), .Down(out_1));
endmodule

module Controller (
);

  wire _0_b_out, _1_a_out, _2_b_prime_out, and_2_out, button_1_out, cdm_8_mark5_1_p4, cdm_8_mark5_1_p5,
       cdm_8_mark5_1_p7, cdm_8_mark5_1_p8, cdm_8_mark5_1_p9, cdm_8_mark5_1_p10, cdm_8_mark5_1_p11,
       cdm_8_mark5_1_p12, cdm_8_mark5_1_p13, clk, decoder_1_out0, decoder_1_out1, decoder_2_out0,
       decoder_2_out2, IAck, IO_2_out, IOsel, IRQ, not_1_out, not_2_out, or_1_out, READwrite;
  wire [1:0] nor_1_out, register_2_q;
  wire [2:0] vec;
  wire [3:0] IOaddr;
  wire [7:0] cdm_8_mark5_1_p16, cdm_8_mark5_1_p17, IOdat, register_1_q;
  wire [7:4] cdm_8_mark5_1_p15;

  Clock clock_1 (.out(clk));
  // Probe on cdm_8_mark5_1_p8
  // Probe on cdm_8_mark5_1_p7
  // Probe on cdm_8_mark5_1_p5
  // Probe on cdm_8_mark5_1_p9
  // Probe on cdm_8_mark5_1_p4
  and and_1 (IOsel, cdm_8_mark5_1_p15[4], cdm_8_mark5_1_p15[5], cdm_8_mark5_1_p15[6], cdm_8_mark5_1_p15[7], decoder_1_out1);
  // Probe on cdm_8_mark5_1_p10
  // Probe on cdm_8_mark5_1_p11
  // CdM_8_mark5 cdm_8_mark5_1: pin names not known; wires that end beside it: IRQ, vec, IAck, cdm_8_mark5_1_p4, cdm_8_mark5_1_p5, clk, cdm_8_mark5_1_p7, cdm_8_mark5_1_p8, cdm_8_mark5_1_p9, cdm_8_mark5_1_p10, cdm_8_mark5_1_p11, cdm_8_mark5_1_p12, cdm_8_mark5_1_p13, READwrite, {cdm_8_mark5_1_p15, IOaddr}, cdm_8_mark5_1_p16, cdm_8_mark5_1_p17
  Decoder #(.disabled(0)) decoder_1 (
    .out0(decoder_1_out0), .out1(decoder_1_out1), .sel(cdm_8_mark5_1_p12), .en(cdm_8_mark5_1_p13));
  not not_1 (not_1_out, READwrite);
  assign IOdat = not_1_out ? cdm_8_mark5_1_p16 : 8'bz;  // Controlled_Buffer controlled_buffer_1
  assign cdm_8_mark5_1_p17 = READwrite ? IOdat : 8'bz;  // Controlled_Buffer controlled_buffer_2
  // Probe on {cdm_8_mark5_1_p15, IOaddr}
  and and_2 (and_2_out, decoder_1_out1, ~IOsel);  // AND_Gate
  not not_2 (not_2_out, clk);
  // Probe on IOdat
  RAM ram_1 (
    .addr({cdm_8_mark5_1_p15, IOaddr}), .data(IOdat), .sel(and_2_out), .clk(not_2_out), .ld(READwrite));  // open: clr
  ROM rom_1 (.addr({cdm_8_mark5_1_p15, IOaddr}), .data(IOdat), .sel(decoder_1_out0));
  and IO_2 (IO_2_out, IOsel, ~IOaddr[0], ~IOaddr[2], ~IOaddr[3]);  // AND_Gate
  Register #(.trigger("falling")) register_1 (.D(IOdat), .en(IO_2_out), .Q(register_1_q), .clk(clk));  // open: clr
  DotMatrix #(.matrixcols(1), .matrixrows(8)) dotmatrix_1 (.col0(register_1_q));
  assign vec = IAck ? 3'b001 : 3'bz;  // Controlled_Buffer controlled_buffer_3
  RowsPlate rowsplate_1 ();  // open: tick, Pressed_1, Pressed_2, Pressed_3, Pressed_4, Pressed_5, Pressed_6, Pressed_7, Pressed_8, Pressed_9, Pressed_10, Pressed_11, Pressed_12, Pressed_13, Pressed_14, Pressed_15, out_1, out_2, out_3, out_4, out_5, out_6, out_7, out_8, out_9, out_10, out_11, out_12, out_13, out_14, out_15
  Decoder #(.select(2), .enable("false")) decoder_2 (
    .out0(decoder_2_out0), .out1(IRQ), .out2(decoder_2_out2), .sel(register_2_q));  // open: out3
  Button button_1 (.out(button_1_out));
  and _0_b (_0_b_out, button_1_out, decoder_2_out0);
  and _1_a (_1_a_out, IAck, IRQ);
  and _2_b_prime (_2_b_prime_out, ~button_1_out, decoder_2_out2);  // AND_Gate
  nor nor_1 (nor_1_out[0], register_2_q[0], register_2_q[1]);
  and and_3 (nor_1_out[1], register_2_q[0], ~register_2_q[1]);  // AND_Gate
  or or_1 (or_1_out, _0_b_out, _1_a_out, _2_b_prime_out);
  Register #(.width(2), .trigger("falling")) register_2 (
    .D(nor_1_out), .en(or_1_out), .Q(register_2_q), .clk(clk));  // open: clr

  // Notes on the sheet:
  //   contents of rom_1 (hex, n*v repeats v):
  //   cd f0 d0 9 c0 d0 80 c0 d9 d3 10 d0 f2 3a a e1 14 2f ee 15 93 e3 19 d3 10 a3 ee e 82 d9 212*0 1c
  //   garland
  //   direction
  //   0->1->2->0
endmodule
